// Logisim project FSM.circ as structural Verilog: 2 circuits, main circuit main
module main (
  input  DIN,
  input  RST,
  output [7:0] DOUT,
  output DOUT_VLD
);

  wire and_1_out, and_2_out, and_3_out, and_4_out, and_5_out, and_6_out, and_7_out, and_8_out, and_9_out,
       and_10_out, and_11_out, CLK_out, comparator_1_eq, comparator_2_eq, d_ff_1_q, d_ff_2_q, d_ff_3_q,
       d_ff_4_q, d_ff_5_q, d_ff_6_q, d_ff_7_q, d_ff_8_q, d_ff_9_q, d_ff_10_q, decoder_1_out0, decoder_1_out1,
       decoder_1_out2, decoder_1_out3, decoder_1_out4, decoder_1_out5, decoder_1_out6, decoder_1_out7,
       FSM_cnt_en, FSM_rx_en, not_1_out, not_2_out, not_3_out, not_4_out, or_1_out, or_2_out, or_3_out;
  wire [3:0] CNT_OF_BITS_q, subtractor_1_out;
  wire [4:0] CNT_OF_CLK_q;
  wire [7:0] adder_1_out, adder_2_out, adder_3_out, adder_4_out, adder_5_out, adder_6_out, adder_7_out,
       bit_extender_1_out, bit_extender_2_out, bit_extender_3_out, bit_extender_4_out, bit_extender_5_out,
       bit_extender_6_out, bit_extender_7_out, bit_extender_8_out, shifter_1_out, shifter_2_out,
       shifter_3_out, shifter_4_out, shifter_5_out, shifter_6_out, shifter_7_out;

  Clock CLK (.out(CLK_out));
  not not_1 (not_1_out, CLK_out);
  and and_1 (and_1_out, and_10_out, CLK_out);
  D_Flip_Flop d_ff_1 (.clk(not_1_out), .D(d_ff_2_q), .Q(d_ff_1_q), .reset(CLK_out));  // open: Qn, preset, en
  D_Flip_Flop d_ff_2 (.clk(and_10_out), .D(1'b1), .Q(d_ff_2_q), .reset(d_ff_1_q));  // open: Qn, preset, en
  Counter #(.width(4), .max('hf)) CNT_OF_BITS (
    .D(4'b0001), .Q(CNT_OF_BITS_q), .clk(and_1_out), .clr(not_2_out));  // open: load, count, carry
  Counter #(.width(5), .max('h1f)) CNT_OF_CLK (
    .D(5'b00001), .Q(CNT_OF_CLK_q), .clk(CLK_out), .clr(or_1_out));  // open: load, count, carry
  or or_1 (or_1_out, and_10_out, not_2_out);
  Decoder #(.select(4)) decoder_1 (
    .out0(decoder_1_out0), .out1(decoder_1_out1), .out2(decoder_1_out2), .out3(decoder_1_out3),
    .out4(decoder_1_out4), .out5(decoder_1_out5), .out6(decoder_1_out6), .out7(decoder_1_out7),
    .sel(subtractor_1_out));  // open: out8, out9, out10, out11, out12, out13, out14, out15, en
  Subtractor #(.width(4)) subtractor_1 (.a(CNT_OF_BITS_q), .b(4'b0001), .out(subtractor_1_out));  // open: bin, bout
  Comparator #(.width(5)) comparator_1 (.a(5'b10000), .b(CNT_OF_CLK_q), .eq(comparator_1_eq));  // open: gt, lt
  not not_2 (not_2_out, FSM_cnt_en);
  Comparator #(.width(5)) comparator_2 (.a(5'b10110), .b(CNT_OF_CLK_q), .eq(comparator_2_eq));  // open: gt, lt
  and and_2 (and_2_out, decoder_1_out0, d_ff_1_q, DIN);
  and and_3 (and_3_out, decoder_1_out1, d_ff_1_q, DIN);
  and and_4 (and_4_out, decoder_1_out2, d_ff_1_q, DIN);
  and and_5 (and_5_out, decoder_1_out3, d_ff_1_q, DIN);
  and and_6 (and_6_out, DIN, d_ff_1_q, decoder_1_out4);
  and and_7 (and_7_out, DIN, d_ff_1_q, decoder_1_out5);
  and and_8 (and_8_out, DIN, d_ff_1_q, decoder_1_out6);
  and and_9 (and_9_out, DIN, d_ff_1_q, decoder_1_out7);
  and and_10 (and_10_out, FSM_rx_en, or_2_out);
  or or_2 (or_2_out, comparator_1_eq, comparator_2_eq);
  D_Flip_Flop d_ff_3 (.clk(and_2_out), .D(decoder_1_out0), .Q(d_ff_3_q), .reset(or_3_out));  // open: Qn, preset, en
  D_Flip_Flop d_ff_4 (.clk(and_3_out), .D(decoder_1_out1), .Q(d_ff_4_q), .reset(or_3_out));  // open: Qn, preset, en
  D_Flip_Flop d_ff_5 (.clk(and_4_out), .D(decoder_1_out2), .Q(d_ff_5_q), .reset(or_3_out));  // open: Qn, preset, en
  D_Flip_Flop d_ff_6 (.clk(and_5_out), .D(decoder_1_out3), .Q(d_ff_6_q), .reset(or_3_out));  // open: Qn, preset, en
  D_Flip_Flop d_ff_7 (.clk(and_6_out), .D(decoder_1_out4), .Q(d_ff_7_q), .reset(or_3_out));  // open: Qn, preset, en
  D_Flip_Flop d_ff_8 (.clk(and_7_out), .D(decoder_1_out5), .Q(d_ff_8_q), .reset(or_3_out));  // open: Qn, preset, en
  D_Flip_Flop d_ff_9 (.clk(and_8_out), .D(decoder_1_out6), .Q(d_ff_9_q), .reset(or_3_out));  // open: Qn, preset, en
  D_Flip_Flop d_ff_10 (.clk(and_9_out), .D(decoder_1_out7), .Q(d_ff_10_q), .reset(or_3_out));  // open: Qn, preset, en
  or or_3 (or_3_out, RST, and_11_out);
  assign bit_extender_1_out = {{7{1'b0}}, d_ff_3_q};  // Bit_Extender bit_extender_1
  assign bit_extender_2_out = {{7{1'b0}}, d_ff_4_q};  // Bit_Extender bit_extender_2
  assign bit_extender_3_out = {{7{1'b0}}, d_ff_5_q};  // Bit_Extender bit_extender_3
  assign bit_extender_4_out = {{7{1'b0}}, d_ff_6_q};  // Bit_Extender bit_extender_4
  assign bit_extender_5_out = {{7{1'b0}}, d_ff_7_q};  // Bit_Extender bit_extender_5
  assign bit_extender_6_out = {{7{1'b0}}, d_ff_8_q};  // Bit_Extender bit_extender_6
  assign bit_extender_7_out = {{7{1'b0}}, d_ff_9_q};  // Bit_Extender bit_extender_7
  assign bit_extender_8_out = {{7{1'b0}}, d_ff_10_q};  // Bit_Extender bit_extender_8
  and and_11 (and_11_out, not_4_out, not_3_out);
  not not_3 (not_3_out, FSM_cnt_en);
  Shifter shifter_1 (.in(bit_extender_2_out), .\dist (3'b001), .out(shifter_1_out));
  Shifter shifter_2 (.in(bit_extender_3_out), .\dist (3'b010), .out(shifter_2_out));
  Shifter shifter_3 (.in(bit_extender_4_out), .\dist (3'b011), .out(shifter_3_out));
  Shifter shifter_4 (.in(bit_extender_5_out), .\dist (3'b100), .out(shifter_4_out));
  Shifter shifter_5 (.in(bit_extender_6_out), .\dist (3'b101), .out(shifter_5_out));
  Shifter shifter_6 (.in(bit_extender_7_out), .\dist (3'b110), .out(shifter_6_out));
  Shifter shifter_7 (.in(bit_extender_8_out), .\dist (3'b111), .out(shifter_7_out));
  not not_4 (not_4_out, DOUT_VLD);
  FSM FSM (
    .CNT_OF_BITS(CNT_OF_BITS_q), .CNT_OF_CLK(CNT_OF_CLK_q), .DIN(DIN), .RST(RST), .CNT_EN(FSM_cnt_en),
    .RX_EN(FSM_rx_en), .DOUT_VALID(DOUT_VLD), .CLK(CLK_out));
  Adder adder_1 (.a(bit_extender_1_out), .b(shifter_1_out), .out(adder_1_out));  // open: cin, cout
  Adder adder_2 (.a(shifter_2_out), .b(shifter_3_out), .out(adder_2_out));  // open: cin, cout
  Adder adder_3 (.a(shifter_4_out), .b(shifter_5_out), .out(adder_3_out));  // open: cin, cout
  Adder adder_4 (.a(shifter_6_out), .b(shifter_7_out), .out(adder_4_out));  // open: cin, cout
  Adder adder_5 (.a(adder_1_out), .b(adder_2_out), .out(adder_5_out));  // open: cin, cout
  Adder adder_6 (.a(adder_3_out), .b(adder_4_out), .out(adder_6_out));  // open: cin, cout
  Adder adder_7 (.a(adder_5_out), .b(adder_6_out), .out(adder_7_out));  // open: cin, cout
  Register register_1 (.D(adder_7_out), .Q(DOUT), .clk(DOUT_VLD), .clr(RST));  // open: en

  // Notes on the sheet:
  //   CNT_OF_BITS
  //   CNT_OF_CLK
  //   CLK
  //   DIN
  //   RST
  //   CNT_EN
  //   RX_EN
  //   DOUT_VALID
endmodule

module FSM (
  input  [3:0] CNT_OF_BITS,
  input  [4:0] CNT_OF_CLK,
  input  CLK,
  input  DIN,
  input  RST,
  output CNT_EN,
  output RX_EN,
  output DOUT_VALID
);

  wire and_1_out, and_2_out, and_3_out, and_4_out, and_5_out, and_6_out, and_7_out, and_8_out,
       comparator_1_eq, comparator_2_eq, d_ff_1_q, d_ff_2_q, not_1_out, not_2_out, not_3_out, not_4_out,
       or_1_out, or_2_out, or_4_out, or_5_out;

  not not_1 (not_1_out, DOUT_VALID);
  not not_2 (not_2_out, RX_EN);
  and and_1 (and_1_out, not_1_out, not_2_out, not_3_out, DIN);
  not not_3 (not_3_out, d_ff_2_q);
  not not_4 (not_4_out, DIN);
  D_Flip_Flop d_ff_1 (.clk(CLK), .D(or_1_out), .Q(d_ff_1_q), .preset(RST));  // open: Qn, en, reset
  or or_1 (or_1_out, and_1_out, and_8_out);
  and and_2 (and_2_out, d_ff_1_q, not_4_out);
  and and_3 (and_3_out, CLK, d_ff_1_q);
  Comparator #(.width(5)) comparator_1 (.a(CNT_OF_CLK), .b(5'b10110), .eq(comparator_1_eq));  // open: gt, lt
  and and_4 (and_4_out, comparator_1_eq, d_ff_2_q);
  or or_2 (or_2_out, RX_EN, and_3_out);
  D_Flip_Flop d_ff_2 (.clk(or_2_out), .D(and_2_out), .Q(d_ff_2_q), .reset(RST));  // open: Qn, preset, en
  or or_3 (CNT_EN, d_ff_2_q, RX_EN);
  and and_5 (and_5_out, CLK, d_ff_2_q);
  Comparator #(.width(4)) comparator_2 (.a(CNT_OF_BITS), .b(4'b1000), .eq(comparator_2_eq));  // open: gt, lt
  and and_6 (and_6_out, comparator_2_eq, RX_EN);
  or or_4 (or_4_out, DOUT_VALID, and_5_out);
  D_Flip_Flop d_ff_3 (.clk(or_4_out), .D(and_4_out), .Q(RX_EN), .reset(RST));  // open: Qn, preset, en
  and and_7 (and_7_out, CLK, RX_EN);
  or or_5 (or_5_out, d_ff_1_q, and_7_out);
  D_Flip_Flop d_ff_4 (.clk(or_5_out), .D(and_6_out), .Q(DOUT_VALID), .reset(RST));  // open: Qn, preset, en
  and and_8 (and_8_out, DIN, DOUT_VALID);

  // Notes on the sheet:
  //   IDLE
  //   START_BIT
  //   DATA_BITS
  //   STOP_BIT
endmodule
